// Logisim project final project_Guo.circ as structural Verilog: 13 circuits, main circuit main
module main (
  output [15:0] out_1,
  output [15:0] out_2,
  output [15:0] out_3,
  output [15:0] out_4,
  output [15:0] out_5,
  output [15:0] out_6,
  output [15:0] out_7,
  output [15:0] out_8,
  output [4:0] out_9,
  output [15:0] out_10,
  output [15:0] out_11,
  output [15:0] out_12,
  output [4:0] out_13,
  output [15:0] out_14,
  output [15:0] out_15,
  output [4:0] s_z_v_c_cb,
  output [15:0] out_17,
  output [15:0] out_18,
  output [15:0] out_19,
  output [15:0] out_20,
  output [15:0] out_21
);

  wire and_1_out, and_2_out, and_3_out, and_4_out, branch, call_return, clock, comparator_1_eq,
       comparator_3_eq, comparator_4_eq, comparator_5_eq, comparator_6_eq, comparator_7_eq, comparator_8_eq,
       comparator_9_eq, not_write, operation_control_1_halt, or_2_out, or_3_out, or_4_out, store, we_branch;
  wire [3:0] a, b, d, multiplexer_3_out, multiplexer_4_out, multiplexer_5_out, op_select, wa_a;
  wire [3:3] comparator_10_eq;
  wire [7:0] multiplexer_8_out;
  wire [15:0] adder_1_out, adder_2_out, b_d, branching_control_1_out_7, current_PC, loaded_value,
       multiplexer_1_out, multiplexer_7_out, read_b, to_be_loaded;

  Comparator #(.width(3), .mode("unsigned")) comparator_1 (
    .a(3'b000), .b(op_select[3:1]), .eq(comparator_1_eq));  // open: gt, lt
  or or_1 (we_branch, and_1_out, call_return);
  and and_1 (and_1_out, branch, comparator_1_eq);
  Comparator #(.width(4), .mode("unsigned")) comparator_2 (
    .a(op_select), .b(4'b0010), .eq(call_return));  // open: gt, lt
  PC_Register pc_register_1 (
    .in_2(operation_control_1_halt), .out_5(current_PC), .in_3(clock), .in_1(multiplexer_1_out),
    .in_4(we_branch));
  ROM #(.addrWidth(16), .dataWidth(16)) rom_1 (.addr(current_PC), .data(out_15));  // open: sel
  Multiplexer #(.width(16)) multiplexer_1 (
    .in0(branching_control_1_out_7), .in1(read_b), .out(multiplexer_1_out), .sel(call_return));  // open: en
  Operation_Control operation_control_1 (
    .in_1(out_15), .Halt(operation_control_1_halt), .Op_Select(op_select), .out_5({a, b}), .write_address(d));
  Multiplexer #(.width(4)) multiplexer_2 (.in0(d), .in1(a), .out(wa_a), .sel(call_return));  // open: en
  Branching_Control branching_control_1 (
    .in_2(b_d), .o({a, b}), .b_8_11(d), .b_12(op_select[0]), .cb(s_z_v_c_cb),
    .out_7(branching_control_1_out_7), .in_1(current_PC), .branch(branch));
  Comparator #(.width(4), .mode("unsigned")) comparator_3 (.a(a), .b(4'b0111), .eq(comparator_3_eq));  // open: gt, lt
  Comparator #(.width(4), .mode("unsigned")) comparator_4 (.a(a), .b(4'b0110), .eq(comparator_4_eq));  // open: gt, lt
  Multiplexer #(.select(4), .width(4)) multiplexer_3 (
    .in0(b), .in1(b), .in2(a), .in3(multiplexer_5_out), .in4(a), .in5(a), .in6(a), .in7(a), .in8(a), .in9(a),
    .in10(a), .in11(a), .in12(a), .in13(a), .in14(d), .in15(d), .out(multiplexer_3_out), .sel(op_select));  // open: en
  Multiplexer #(.select(4), .width(4)) multiplexer_4 (
    .in0(b), .in1(b), .in2(b), .in3(b), .in4(b), .in5(b), .in6(b), .in7(b), .in8(b), .in9(b), .in10(b),
    .in11(b), .in12(b), .in13(b), .in14(d), .in15(d), .out(multiplexer_4_out), .sel(op_select));  // open: en
  Comparator #(.width(4), .mode("unsigned")) comparator_5 (
    .a(op_select), .b(4'b0011), .eq(comparator_5_eq));  // open: gt, lt
  Comparator #(.width(1), .mode("unsigned")) comparator_6 (.a(a[3]), .b(1'b1), .eq(comparator_6_eq));  // open: gt, lt
  and and_2 (and_2_out, b[3], comparator_3_eq);
  or or_2 (or_2_out, comparator_3_eq, comparator_4_eq);
  Multiplexer #(.width(4)) multiplexer_5 (.in0(b), .in1(d), .out(multiplexer_5_out), .sel(and_3_out));  // open: en
  and and_3 (and_3_out, comparator_5_eq, or_3_out);
  and and_4 (and_4_out, comparator_5_eq, or_4_out);
  or or_3 (or_3_out, comparator_6_eq, or_2_out);
  or or_4 (or_4_out, and_2_out, comparator_4_eq);
  Comparator #(.width(4), .mode("unsigned")) comparator_7 (
    .a(op_select), .b(4'b0110), .eq(comparator_7_eq));  // open: gt, lt
  Comparator #(.width(4), .mode("unsigned")) comparator_8 (
    .a(op_select), .b(4'b0111), .eq(comparator_8_eq));  // open: gt, lt
  or or_5 (not_write, and_4_out, store, comparator_1_eq);
  Adder #(.width(16)) adder_1 (.a(read_b), .b({{11{1'b0}}, op_select[0], a}), .out(adder_1_out));  // open: cin, cout
  or or_6 (store, comparator_7_eq, comparator_8_eq);
  Adder #(.width(16)) adder_2 (.a(current_PC), .b(16'h1), .out(adder_2_out));  // open: cin, cout
  Flags flags_1 (.in_1(out_13), .out_4(s_z_v_c_cb), .in_3(clock), .in_2(we_branch));
  Register_File register_file_1 (
    .RA_1(multiplexer_3_out), .RA_2(multiplexer_4_out), .WA(wa_a), .out_27(b_d), .in_3(multiplexer_7_out),
    .out_11(out_1), .out_12(out_2), .out_13(out_3), .out_14(out_4), .out_15(out_6), .out_16(out_7),
    .out_17(out_8), .out_18(out_10), .out_19(out_11), .out_20(out_12), .out_21(out_14), .out_22(out_17),
    .out_23(out_18), .out_24(out_19), .out_25(out_20), .out_26(out_21), .in_10(clock), .not_write(not_write),
    .WA_2(b), .WD_2(adder_2_out), .in_2(b_d), .out_28(read_b), .write(call_return));
  Multiplexer #(.width(5)) multiplexer_6 (
    .in0(out_9), .in1({loaded_value[15], comparator_10_eq[3], out_9[2:0]}), .out(out_13),
    .sel(comparator_9_eq));  // open: en
  Clock clock_1 (.out(clock));
  ALSU alsu_1 (
    .operand_1_main(b_d), .in_2(read_b), .op_code(op_select), .out_7(out_5), .current_flags(s_z_v_c_cb),
    ._0011_op__0_7({a, b}), .flags(out_9), .d_8_11(d));
  HERA_Memory hera_memory_1 (
    .in_1(adder_1_out), .store(to_be_loaded), .clock(clock), .out_5(loaded_value), .in_4(store));
  Multiplexer #(.select(4), .width(16)) multiplexer_7 (
    .in0(out_5), .in1(out_5), .in2(out_20), .in3(out_5), .in4(loaded_value), .in5(loaded_value), .in6(out_5),
    .in7(out_5), .in8(out_5), .in9(out_5), .in10(out_5), .in11(out_5), .in12(out_5), .in13(out_5),
    .in14({{9{multiplexer_8_out[7]}}, multiplexer_8_out[6:0]}), .in15({multiplexer_8_out, b_d[7:0]}),
    .out(multiplexer_7_out), .sel(op_select));  // open: en
  Multiplexer #(.select(4), .width(8)) multiplexer_8 (
    .in14({a, b}), .in15({a, b}), .out(multiplexer_8_out), .sel(op_select));  // open: in0, in1, in2, in3, in4, in5, in6, in7, in8, in9, in10, in11, in12, in13, en
  Comparator #(.width(3), .mode("unsigned")) comparator_9 (
    .a(op_select[3:1]), .b(3'b010), .eq(comparator_9_eq));  // open: gt, lt
  Comparator #(.width(16), .mode("unsigned")) comparator_10 (
    .a(loaded_value), .b({16{1'b0}}), .eq(comparator_10_eq[3]));  // open: gt, lt
  // Probe on out_1
  // Probe on out_2
  // Probe on out_3
  // Probe on out_4
  // Probe on out_6
  // Probe on out_7
  // Probe on out_8
  // Probe on out_10
  // Probe on out_11
  // Probe on out_12
  // Probe on out_14
  // Probe on out_17
  // Probe on out_18
  // Probe on out_19
  // Probe on out_20
  // Probe on out_21
  Multiplexer #(.select(4), .width(16)) multiplexer_9 (
    .in0(out_1), .in1(out_2), .in2(out_3), .in3(out_4), .in4(out_6), .in5(out_7), .in6(out_8), .in7(out_10),
    .in8(out_11), .in9(out_12), .in10(out_14), .in11(out_17), .in12(out_18), .in13(out_19), .in14(out_20),
    .in15(out_21), .out(to_be_loaded), .sel(d));  // open: en
  // Probe on out_1
  // Probe on out_2
  // Probe on out_3
  // Probe on out_4
  // Probe on out_6
  // Probe on out_7
  // Probe on out_8
  // Probe on out_10
  // Probe on out_11
  // Probe on out_12
  // Probe on out_14
  // Probe on out_17
  // Probe on out_18
  // Probe on out_19
  // Probe on out_20
  // Probe on out_21

  // Other names for the same wires on the sheet: o[7:0] = {a, b}; _0[15:0] = out_1; _1[15:0] = out_2;
  //   _2[15:0] = out_3; _3[15:0] = out_4; _4[15:0] = out_6; _5[15:0] = out_7; _6[15:0] = out_8; _7[15:0] = out_10;
  //   _8[15:0] = out_11; _9[15:0] = out_12; _10[15:0] = out_14; _11[15:0] = out_17; _12[15:0] = out_18;
  //   _13[15:0] = out_19; _14[15:0] = out_20; _15[15:0] = out_21; flags[4:0] = s_z_v_c_cb; read_a[15:0] = b_d

  // Notes on the sheet:
  //   program ROM
  //   load data to pc
  //   call/return?
  //   contents of rom_1 (hex, n*v repeats v):
  //   3160 e207 f200 e305 f300 e409 f400 b023 204 b034 207 8 b024 202 5 9520 5 9530 3 9540 1
  //   current Rb
  //   select write address for a
  //   d
  //   4-7
  //   0-3
  //   4-6
  //   branch to that line of command and keeps adding one to that # of line if it's not branching anymore
  //   op code
  //   d
  //   b
  //   d
  //   inc/dec(read d)
  //   read 1/a
  //   read 2/b
  //    only read d 
  //   write data
  //   operand 1
  //   operand 2
  //   op code
  //   0011 op
  //   not change flags
  //   store/not write registers
  //   low 8-bit
  //   SETLO
  //   load,change flags
  //   SETHI
  //   high 8-bit
  //   R0
  //   R1
  //   R2
  //   R3
  //   R4
  //   R5
  //   R6
  //   R7
  //   R8
  //   R9
  //   R10
  //   R11
  //   R12
  //   R13
  //   R14
  //   R15
endmodule

module Operation_Control (
  input  [15:0] in_1,
  output Halt,
  output [3:0] Op_Select,
  output [3:0] write_address,
  output [7:0] out_5
);

  Comparator #(.width(16)) comparator_1 (.a(in_1), .b({16{1'b0}}), .eq(Halt));  // open: gt, lt

  assign Op_Select = in_1[15:12];
  assign out_5 = in_1[7:0];
  assign write_address = in_1[11:8];

  // Notes on the sheet:
  //   op code/read address
endmodule

module ALSU (
  input  [15:0] operand_1_main,
  input  [15:0] in_2,
  input  [3:0] op_code,
  input  [4:0] current_flags,
  input  [7:0] _0011_op__0_7,
  input  [3:0] d_8_11,
  output [15:0] out_7,
  output [4:0] flags
);

  wire add_v, adder_2_cout, adder_3_cout, and_2_out, and_3_out, and_4_out, and_5_out, and_7_out, and_8_out,
       and_9_out, and_10_out, and_11_out, and_12_out, and_13_out, and_14_out, ASL_v, comparator_1_eq,
       comparator_1_lt, comparator_2_eq, comparator_3_eq, comparator_4_eq, comparator_5_eq, comparator_7_eq,
       comparator_8_eq, comparator_9_lt, comparator_10_gt, dec_v, inc_v, mul_v, multiplexer_4_out,
       multiplexer_9_out, multiplexer_10_out, multiplexer_11_out, multiplexer_13_out, multiplexer_14_out,
       not_1_out, not_2_out, not_3_out, not_4_out, not_5_out, not_6_out, not_7_out, not_8_out, not_9_out,
       not_10_out, not_11_out, not_12_out, not_14_out, not_15_out, not_16_out, not_17_out, not_18_out,
       not_19_out, not_20_out, not_21_out, or_2_out, or_3_out, or_4_out, or_5_out, sub_v, subtractor_1_bout,
       subtractor_2_bout;
  wire [0:0] multiplexer_1_out;
  wire [3:1] multiplexer_7_out;
  wire [4:0] and_6_out, flag_result, multiplexer_15_out, multiplexer_16_out, not_13_out, or_7_out;
  wire [15:0] and_1_out, high_16, inc_dec, multiplexer_2_out, multiplexer_3_out, multiplexer_6_out,
       multiplexer_8_out, or_1_out, output_add, output_ASL, output_dec, output_inc, output_sub, result,
       shifter_1_out, shifter_2_out, shifter_3_out, xor_1_out;

  Multiplexer multiplexer_1 (
    .in0(current_flags[1]), .in1(1'b0), .out(multiplexer_1_out[0]), .sel(current_flags[0]));  // open: en
  Multiplexer #(.select(5), .width(16)) multiplexer_2 (
    .in0(result), .in1(result), .in2(result), .in3(result), .in4(result), .in5(result), .in6(result),
    .in7(result), .in8(result), .in9(result), .in10(result), .in11(result), .in12(result), .in13(result),
    .in14(result), .in15(result), .in16(high_16), .in17(result), .in18(result), .in19(result), .in20(result),
    .in21(result), .in22(result), .in23(result), .in24(result), .in25(result), .in26(result), .in27(result),
    .in28(result), .in29(result), .in30(result), .in31(result), .out(multiplexer_2_out), .sel(current_flags));  // open: en
  Multiplier #(.width(16)) multiplier_1 (.a(operand_1_main), .b(in_2), .out(result), .cout(high_16));  // open: cin
  Adder #(.width(16)) adder_1 (.a({{10{1'b0}}, _0011_op__0_7[5:0]}), .b(16'h1), .out(inc_dec));  // open: cin, cout
  Shifter #(.width(16)) shifter_1 (.in(operand_1_main), .\dist (4'b1000), .out(shifter_1_out));
  Shifter #(.width(16), .shift("lr")) shifter_2 (.in(operand_1_main), .\dist (4'b1000), .out(shifter_2_out));
  Shifter #(.width(16), .shift("ar")) shifter_3 (.in(operand_1_main), .\dist (4'b0001), .out(shifter_3_out));
  assign and_1_out = operand_1_main & in_2;  // AND_Gate and_1, 16 bits wide
  assign or_1_out = operand_1_main | in_2;  // OR_Gate or_1, 16 bits wide
  assign xor_1_out = operand_1_main ^ in_2;  // XOR_Gate xor_1, 16 bits wide
  Adder #(.width(16)) adder_2 (
    .a(operand_1_main), .b(in_2), .out(output_add), .cin(multiplexer_1_out[0]), .cout(adder_2_cout));
  Subtractor #(.width(16)) subtractor_1 (
    .a(operand_1_main), .b(in_2), .out(output_sub), .bin(multiplexer_1_out[0]), .bout(subtractor_1_bout));
  Adder #(.width(16)) adder_3 (.a(operand_1_main), .b(inc_dec), .out(output_inc), .cout(adder_3_cout));  // open: cin
  Subtractor #(.width(16)) subtractor_2 (
    .a(operand_1_main), .b(inc_dec), .out(output_dec), .bout(subtractor_2_bout));  // open: bin
  not not_1 (not_1_out, subtractor_1_bout);
  not not_2 (not_2_out, subtractor_2_bout);
  Adder #(.width(16)) adder_4 (
    .a(operand_1_main), .b(operand_1_main), .out(output_ASL), .cin(multiplexer_1_out[0]));  // open: cout
  Comparator #(.width(32), .mode("unsigned")) comparator_1 (
    .a(32'h10000), .b({high_16, result}), .eq(comparator_1_eq), .lt(comparator_1_lt));  // open: gt
  Multiplexer #(.select(2), .width(16)) multiplexer_3 (
    .in2(output_inc), .in3(output_dec), .out(multiplexer_3_out), .sel(_0011_op__0_7[7:6]));  // open: in0, in1, en
  or or_2 (or_2_out, comparator_1_eq, comparator_1_lt);
  Multiplexer #(.select(2)) multiplexer_4 (
    .in2(adder_3_cout), .in3(not_2_out), .out(multiplexer_4_out), .sel(_0011_op__0_7[7:6]));  // open: in0, in1, en
  Multiplexer #(.select(4), .width(16)) multiplexer_5 (
    .in0({16{1'b0}}), .in3(multiplexer_8_out), .in8(and_1_out), .in9(or_1_out), .in10(output_add),
    .in11(output_sub), .in12(multiplexer_2_out), .in13(xor_1_out), .out(out_7), .sel(op_code));  // open: in1, in2, in4, in5, in6, in7, in14, in15, en
  Multiplexer #(.select(4), .width(16)) multiplexer_6 (
    .in0({operand_1_main[14:0], multiplexer_1_out[0]}), .in1({multiplexer_1_out[0], operand_1_main[15:1]}),
    .in2(shifter_1_out), .in3(shifter_2_out), .in4({operand_1_main[14:0], multiplexer_1_out[0]}),
    .in5(shifter_3_out), .in7({{11{1'b0}}, current_flags}), .out(multiplexer_6_out), .sel(_0011_op__0_7[7:4]));  // open: in6, in8, in9, in10, in11, in12, in13, in14, in15, en
  Multiplexer #(.select(4)) multiplexer_7 (
    .in3(multiplexer_10_out), .in8(current_flags[1]), .in9(current_flags[1]), .in10(adder_2_cout),
    .in11(not_1_out), .in12(or_2_out), .in13(current_flags[1]), .out(multiplexer_7_out[1]), .sel(op_code));  // open: in0, in1, in2, in4, in5, in6, in7, in14, in15, en
  Multiplexer #(.width(16)) multiplexer_8 (
    .in0(multiplexer_6_out), .in1(multiplexer_3_out), .out(multiplexer_8_out), .sel(_0011_op__0_7[7]));  // open: en
  Multiplexer #(.select(4)) multiplexer_9 (
    .in0(operand_1_main[15]), .in1(operand_1_main[0]), .in4(operand_1_main[15]), .out(multiplexer_9_out),
    .sel(_0011_op__0_7[7:4]));  // open: in2, in3, in5, in6, in7, in8, in9, in10, in11, in12, in13, in14, in15, en
  Multiplexer multiplexer_10 (
    .in0(multiplexer_9_out), .in1(multiplexer_4_out), .out(multiplexer_10_out), .sel(_0011_op__0_7[7]));  // open: en
  Multiplexer #(.select(4)) multiplexer_11 (
    .in0(current_flags[2]), .in1(current_flags[2]), .in2(current_flags[2]), .in3(current_flags[2]),
    .in4(ASL_v), .in5(current_flags[2]), .out(multiplexer_11_out), .sel(_0011_op__0_7[7:4]));  // open: in6, in7, in8, in9, in10, in11, in12, in13, in14, in15, en
  Comparator #(.width(4), .mode("unsigned")) comparator_2 (
    .a(op_code), .b(4'b0011), .eq(comparator_2_eq));  // open: gt, lt
  Comparator #(.width(4), .mode("unsigned")) comparator_3 (
    .a(4'b0110), .b(_0011_op__0_7[7:4]), .eq(comparator_3_eq));  // open: gt, lt
  Comparator #(.width(4), .mode("unsigned")) comparator_4 (
    .a(op_code), .b(4'b0011), .eq(comparator_4_eq));  // open: gt, lt
  Comparator #(.width(4), .mode("unsigned")) comparator_5 (
    .a(4'b0111), .b(_0011_op__0_7[7:4]), .eq(comparator_5_eq));  // open: gt, lt
  Comparator #(.width(16)) comparator_6 (.a(out_7), .b({16{1'b0}}), .eq(multiplexer_7_out[3]));  // open: gt, lt
  and and_2 (and_2_out, comparator_5_eq, comparator_2_eq);
  Multiplexer #(.select(4)) multiplexer_12 (
    .in3(multiplexer_14_out), .in8(current_flags[2]), .in9(current_flags[2]), .in10(add_v), .in11(sub_v),
    .in12(mul_v), .in13(current_flags[2]), .out(multiplexer_7_out[2]), .sel(op_code));  // open: in0, in1, in2, in4, in5, in6, in7, in14, in15, en
  and and_3 (and_3_out, comparator_3_eq, comparator_4_eq);
  or or_3 (or_3_out, not_3_out, or_5_out);
  not not_3 (not_3_out, _0011_op__0_7[3]);
  Multiplexer #(.select(2)) multiplexer_13 (
    .in0(1'b0), .in1(1'b0), .in2(inc_v), .in3(dec_v), .out(multiplexer_13_out), .sel(_0011_op__0_7[7:6]));  // open: en
  Multiplexer multiplexer_14 (
    .in0(multiplexer_11_out), .in1(multiplexer_13_out), .out(multiplexer_14_out), .sel(_0011_op__0_7[7]));  // open: en
  Multiplexer #(.width(5)) multiplexer_15 (
    .in0(operand_1_main[4:0]), .in1(current_flags), .out(multiplexer_15_out), .sel(or_3_out));  // open: en
  Multiplexer #(.width(5)) multiplexer_16 (
    .in0(multiplexer_15_out), .in1(flag_result), .out(multiplexer_16_out), .sel(and_3_out));  // open: en
  not not_4 (not_4_out, operand_1_main[15]);
  not not_5 (not_5_out, in_2[15]);
  not not_6 (not_6_out, output_add[15]);
  Multiplexer #(.width(5)) multiplexer_17 (
    .in0({out_7[15], multiplexer_7_out, current_flags[0]}), .in1(multiplexer_16_out), .out(flags),
    .sel(or_4_out));  // open: en
  Comparator #(.width(4), .mode("unsigned")) comparator_7 (
    .a(op_code), .b(4'b0000), .eq(comparator_7_eq));  // open: gt, lt
  Comparator #(.width(4), .mode("unsigned")) comparator_8 (
    .a(op_code), .b(4'b0001), .eq(comparator_8_eq));  // open: gt, lt
  or or_4 (or_4_out, and_3_out, and_2_out);
  or or_5 (or_5_out, comparator_7_eq, comparator_8_eq);
  and and_4 (and_4_out, operand_1_main[15], in_2[15], not_6_out);
  and and_5 (and_5_out, not_4_out, not_5_out, output_add[15]);
  or or_6 (add_v, and_4_out, and_5_out);
  not not_7 (not_7_out, operand_1_main[15]);
  not not_8 (not_8_out, inc_dec[15]);
  not not_9 (not_9_out, output_inc[15]);
  not not_10 (not_10_out, operand_1_main[15]);
  not not_11 (not_11_out, inc_dec[15]);
  not not_12 (not_12_out, output_dec[15]);
  assign not_13_out = ~{_0011_op__0_7[0], _0011_op__0_7[1], _0011_op__0_7[2], _0011_op__0_7[3], d_8_11[0]};  // NOT_Gate not_13, 5 bits wide
  assign and_6_out = not_13_out & current_flags;  // AND_Gate and_6, 5 bits wide
  and and_7 (and_7_out, operand_1_main[15], inc_dec[15], not_9_out);
  and and_8 (and_8_out, not_7_out, not_8_out, output_inc[15]);
  and and_9 (and_9_out, operand_1_main[15], not_11_out, not_12_out);
  and and_10 (and_10_out, not_10_out, inc_dec[15], output_dec[15]);
  Comparator #(.width(32)) comparator_9 (
    .a({high_16, result}), .b(32'h40000000), .lt(comparator_9_lt));  // open: gt, eq
  Comparator #(.width(32)) comparator_10 (
    .a({high_16, result}), .b(32'hc0008000), .gt(comparator_10_gt));  // open: eq, lt
  assign or_7_out = {_0011_op__0_7[0], _0011_op__0_7[1], _0011_op__0_7[2], _0011_op__0_7[3], d_8_11[0]} | current_flags;  // OR_Gate or_7, 5 bits wide
  not not_14 (not_14_out, operand_1_main[15]);
  not not_15 (not_15_out, in_2[15]);
  not not_16 (not_16_out, output_sub[15]);
  or or_8 (inc_v, and_7_out, and_8_out);
  not not_17 (not_17_out, comparator_9_lt);
  not not_18 (not_18_out, comparator_10_gt);
  or or_9 (dec_v, and_9_out, and_10_out);
  or or_10 (mul_v, not_17_out, not_18_out);
  and and_11 (and_11_out, operand_1_main[15], not_15_out, not_16_out);
  and and_12 (and_12_out, not_14_out, in_2[15], output_sub[15]);
  Multiplexer #(.select(3), .width(5)) multiplexer_18 (
    .in0(or_7_out),
    .in2({_0011_op__0_7[0], _0011_op__0_7[1], _0011_op__0_7[2], _0011_op__0_7[3], d_8_11[0]}),
    .in4(and_6_out),
    .in6({_0011_op__0_7[0], _0011_op__0_7[1], _0011_op__0_7[2], _0011_op__0_7[3], current_flags[0]}),
    .out(flag_result), .sel(d_8_11[3:1]));  // open: in1, in3, in5, in7, en
  or or_11 (sub_v, and_11_out, and_12_out);
  not not_19 (not_19_out, operand_1_main[15]);
  not not_20 (not_20_out, operand_1_main[15]);
  not not_21 (not_21_out, output_ASL[15]);
  and and_13 (and_13_out, operand_1_main[15], operand_1_main[15], not_21_out);
  and and_14 (and_14_out, not_19_out, not_20_out, output_ASL[15]);
  or or_12 (ASL_v, and_13_out, and_14_out);

  // Other names for the same wires on the sheet: operand_1[15:0] = operand_1_main; c = current_flags[1];
  //   v = current_flags[2]; output[15:0] = out_7; cb = current_flags[0]; b_3 = _0011_op__0_7[3];
  //   op__0_7[7:0] = _0011_op__0_7; b_4_7[3:0] = _0011_op__0_7[7:4]; operand_2[15:0] = in_2; result[31:16] = high_16

  // Notes on the sheet:
  //   s z v c cb
  //   cb
  //   v
  //   z
  //   s
  //   operand 2
  //   c
  //   carry
  //     operand d
  //   operand b
  //   LSL
  //   LSR
  //   LSL8
  //   LSR8
  //   ASR
  //   increment
  //   decrement
  //   carry
  //   carry
  //   output (to be stored)
  //   carry
  //   s
  //   carry
  //   overflow
  //   z
  //   v
  //   c
  //   overflow
  //   overflow
  //   overflow
  //   overflow for addtion
  //   s z v c cb
  //   op code 2(0-7)
  //   current flags
  //   overflow for increment
  //   flag op
  //   overflow for decrement
  //   overflow for multiplication
  //   v4
  //   v(0-3)
  //   F
  //   overflow for subtraction
  //   v
  //   overflow for ASL
endmodule

module Program_ROM (
  input  [7:0] in_1,
  output [15:0] out_2
);

  ROM #(.dataWidth(16)) rom_1 (.addr(in_1), .data(out_2));  // open: sel
endmodule

module PC_Register (
  input  [15:0] in_1,
  input  in_2,
  input  in_3,
  input  in_4,
  output [15:0] out_5
);

  wire not_1_out, or_1_out;
  wire [15:0] multiplexer_1_out;

  Multiplexer #(.width(16)) multiplexer_1 (.in0(in_1), .in1(out_5), .out(multiplexer_1_out), .sel(in_2));  // open: en
  not not_1 (not_1_out, or_1_out);
  or or_1 (or_1_out, in_2, in_4);
  Counter #(.width(16), .max('hffff)) counter_1 (
    .load(or_1_out), .D(multiplexer_1_out), .count(not_1_out), .Q(out_5), .clk(in_3));  // open: carry, clr
endmodule

module Flags (
  input  [4:0] in_1,
  input  in_2,
  input  in_3,
  output [4:0] out_4
);

  wire not_1_out;

  not not_1 (not_1_out, in_2);
  Register #(.width(5)) register_1 (.D(in_1), .en(not_1_out), .Q(out_4), .clk(in_3));  // open: clr
endmodule

module Register_File (
  input  [15:0] WD_2,
  input  [15:0] in_2,
  input  [15:0] in_3,
  input  [3:0] RA_1,
  input  [3:0] RA_2,
  input  [3:0] WA,
  input  not_write,
  input  [3:0] WA_2,
  input  write,
  input  in_10,
  output [15:0] out_11,
  output [15:0] out_12,
  output [15:0] out_13,
  output [15:0] out_14,
  output [15:0] out_15,
  output [15:0] out_16,
  output [15:0] out_17,
  output [15:0] out_18,
  output [15:0] out_19,
  output [15:0] out_20,
  output [15:0] out_21,
  output [15:0] out_22,
  output [15:0] out_23,
  output [15:0] out_24,
  output [15:0] out_25,
  output [15:0] out_26,
  output [15:0] out_27,
  output [15:0] out_28
);

  wire _0, _1, _2, _3, _4, _5, _6, _7, _8, _9, _10, _11, _12, _13, _15, decoder_1_out0, decoder_1_out1,
       decoder_1_out2, decoder_1_out3, decoder_1_out4, decoder_1_out5, decoder_1_out6, decoder_1_out7,
       decoder_1_out8, decoder_1_out9, decoder_1_out10, decoder_1_out11, decoder_1_out12, decoder_1_out13,
       decoder_1_out14, decoder_1_out15, decoder_2_out0, decoder_2_out1, decoder_2_out2, decoder_2_out3,
       decoder_2_out4, decoder_2_out5, decoder_2_out6, decoder_2_out7, decoder_2_out8, decoder_2_out9,
       decoder_2_out10, decoder_2_out11, decoder_2_out12, decoder_2_out13, decoder_2_out14, decoder_2_out15,
       decoder_3_out1, decoder_3_out2, decoder_3_out3, decoder_3_out4, decoder_3_out5, decoder_3_out6,
       decoder_3_out7, decoder_3_out8, decoder_3_out9, decoder_3_out10, decoder_3_out11, decoder_3_out12,
       decoder_3_out13, decoder_3_out14, decoder_3_out15, not_1_out;
  wire [3:0] multiplexer_1_out;
  wire [15:0] new_memory_cell_1_out_7, new_memory_cell_2_out_7, new_memory_cell_3_out_7,
       new_memory_cell_4_out_7, new_memory_cell_5_out_7, new_memory_cell_6_out_7, new_memory_cell_7_out_7,
       new_memory_cell_8_out_7, new_memory_cell_9_out_7, new_memory_cell_10_out_7, new_memory_cell_11_out_7,
       new_memory_cell_12_out_7, new_memory_cell_13_out_7, new_memory_cell_14_out_7,
       new_memory_cell_15_out_7, new_memory_cell_16_out_7, new_memory_cell_17_out_7,
       new_memory_cell_18_out_7, new_memory_cell_19_out_7, new_memory_cell_20_out_7,
       new_memory_cell_21_out_7, new_memory_cell_22_out_7, new_memory_cell_23_out_7,
       new_memory_cell_24_out_7, new_memory_cell_25_out_7, new_memory_cell_26_out_7,
       new_memory_cell_27_out_7, new_memory_cell_28_out_7, new_memory_cell_29_out_7,
       new_memory_cell_30_out_7, new_memory_cell_31_out_7, new_memory_cell_32_out_7;

  Decoder #(.select(4)) decoder_1 (
    .out0(decoder_1_out0), .out1(decoder_1_out1), .out2(decoder_1_out2), .out3(decoder_1_out3),
    .out4(decoder_1_out4), .out5(decoder_1_out5), .out6(decoder_1_out6), .out7(decoder_1_out7),
    .out8(decoder_1_out8), .out9(decoder_1_out9), .out10(decoder_1_out10), .out11(decoder_1_out11),
    .out12(decoder_1_out12), .out13(decoder_1_out13), .out14(decoder_1_out14), .out15(decoder_1_out15),
    .sel(RA_1));  // open: en
  Decoder #(.select(4)) decoder_2 (
    .out0(decoder_2_out0), .out1(decoder_2_out1), .out2(decoder_2_out2), .out3(decoder_2_out3),
    .out4(decoder_2_out4), .out5(decoder_2_out5), .out6(decoder_2_out6), .out7(decoder_2_out7),
    .out8(decoder_2_out8), .out9(decoder_2_out9), .out10(decoder_2_out10), .out11(decoder_2_out11),
    .out12(decoder_2_out12), .out13(decoder_2_out13), .out14(decoder_2_out14), .out15(decoder_2_out15),
    .sel(RA_2));  // open: en
  not not_1 (not_1_out, not_write);
  Multiplexer #(.width(4)) multiplexer_1 (.in0(4'b0000), .in1(WA_2), .out(multiplexer_1_out), .sel(write));  // open: en
  Decoder #(.select(4)) decoder_3 (
    .out1(decoder_3_out1), .out2(decoder_3_out2), .out3(decoder_3_out3), .out4(decoder_3_out4),
    .out5(decoder_3_out5), .out6(decoder_3_out6), .out7(decoder_3_out7), .out8(decoder_3_out8),
    .out9(decoder_3_out9), .out10(decoder_3_out10), .out11(decoder_3_out11), .out12(decoder_3_out12),
    .out13(decoder_3_out13), .out14(decoder_3_out14), .out15(decoder_3_out15), .sel(WA), .en(not_1_out));  // open: out0
  Decoder #(.select(4)) decoder_4 (
    .out0(_0), .out1(_1), .out2(_2), .out3(_3), .out4(_4), .out5(_5), .out6(_6), .out7(_7), .out8(_8),
    .out9(_9), .out10(_10), .out11(_11), .out12(_12), .out13(_13), .out15(_15), .sel(multiplexer_1_out));  // open: out14, en
  new_memory_cell new_memory_cell_1 (
    .in_2(in_3), .in_3(WD_2), .clock(in_10), .out_7(new_memory_cell_1_out_7), .read(decoder_1_out0));  // open: out_8, write, in_6
  new_memory_cell new_memory_cell_2 (
    .in_2(in_3), .in_3(WD_2), .clock(in_10), .out_7(new_memory_cell_2_out_7), .read(decoder_1_out1),
    .write(decoder_3_out1), .in_6(_1));  // open: out_8
  new_memory_cell new_memory_cell_3 (
    .in_2(in_3), .in_3(WD_2), .clock(in_10), .out_7(new_memory_cell_3_out_7), .read(decoder_1_out2),
    .write(decoder_3_out2), .in_6(_2));  // open: out_8
  new_memory_cell new_memory_cell_4 (
    .in_2(in_3), .in_3(WD_2), .clock(in_10), .out_7(new_memory_cell_4_out_7), .read(decoder_1_out3),
    .write(decoder_3_out3), .in_6(_3));  // open: out_8
  new_memory_cell new_memory_cell_5 (
    .in_2(in_3), .in_3(WD_2), .clock(in_10), .out_7(new_memory_cell_5_out_7), .read(decoder_1_out4),
    .write(decoder_3_out4), .in_6(_4));  // open: out_8
  new_memory_cell new_memory_cell_6 (
    .in_2(in_3), .in_3(WD_2), .clock(in_10), .out_7(new_memory_cell_6_out_7), .read(decoder_1_out5),
    .write(decoder_3_out5), .in_6(_5));  // open: out_8
  new_memory_cell new_memory_cell_7 (
    .in_2(in_3), .in_3(WD_2), .clock(in_10), .out_7(new_memory_cell_7_out_7), .read(decoder_1_out6),
    .write(decoder_3_out6), .in_6(_6));  // open: out_8
  new_memory_cell new_memory_cell_8 (
    .in_2(in_3), .in_3(WD_2), .clock(in_10), .out_7(new_memory_cell_8_out_7), .read(decoder_1_out7),
    .write(decoder_3_out7), .in_6(_7));  // open: out_8
  new_memory_cell new_memory_cell_9 (
    .in_2(in_3), .in_3(WD_2), .clock(in_10), .out_7(new_memory_cell_9_out_7), .read(decoder_1_out8),
    .write(decoder_3_out8), .in_6(_8));  // open: out_8
  new_memory_cell new_memory_cell_10 (
    .in_2(in_3), .in_3(WD_2), .clock(in_10), .out_7(new_memory_cell_10_out_7), .read(decoder_1_out9),
    .write(decoder_3_out9), .in_6(_9));  // open: out_8
  new_memory_cell new_memory_cell_11 (
    .in_2(in_3), .in_3(WD_2), .clock(in_10), .out_7(new_memory_cell_11_out_7), .read(decoder_1_out10),
    .write(decoder_3_out10), .in_6(_10));  // open: out_8
  new_memory_cell new_memory_cell_12 (
    .in_2(in_3), .in_3(WD_2), .clock(in_10), .out_7(new_memory_cell_12_out_7), .read(decoder_1_out11),
    .write(decoder_3_out11), .in_6(_11));  // open: out_8
  new_memory_cell new_memory_cell_13 (
    .in_2(in_3), .in_3(WD_2), .clock(in_10), .out_7(new_memory_cell_13_out_7), .read(decoder_1_out12),
    .write(decoder_3_out12), .in_6(_12));  // open: out_8
  new_memory_cell new_memory_cell_14 (
    .in_2(in_3), .in_3(WD_2), .clock(in_10), .out_7(new_memory_cell_14_out_7), .read(decoder_1_out13),
    .write(decoder_3_out13), .in_6(_13));  // open: out_8
  new_memory_cell new_memory_cell_15 (
    .in_2(in_3), .in_3(in_2), .clock(in_10), .out_7(new_memory_cell_15_out_7), .read(decoder_1_out14),
    .write(decoder_3_out14), .in_6(write));  // open: out_8
  new_memory_cell new_memory_cell_16 (
    .in_2(in_3), .in_3(WD_2), .clock(in_10), .out_7(new_memory_cell_16_out_7), .read(decoder_1_out15),
    .write(decoder_3_out15), .in_6(_15));  // open: out_8
  assign out_27 = new_memory_cell_2_out_7 | new_memory_cell_3_out_7 | new_memory_cell_4_out_7 | new_memory_cell_5_out_7 | new_memory_cell_6_out_7 | new_memory_cell_7_out_7 | new_memory_cell_8_out_7 | new_memory_cell_9_out_7 | new_memory_cell_10_out_7 | new_memory_cell_11_out_7 | new_memory_cell_12_out_7 | new_memory_cell_13_out_7 | new_memory_cell_14_out_7 | new_memory_cell_15_out_7 | new_memory_cell_16_out_7 | new_memory_cell_1_out_7;  // OR_Gate or_1, 16 bits wide
  new_memory_cell new_memory_cell_17 (
    .in_2(in_3), .in_3(WD_2), .clock(in_10), .out_7(new_memory_cell_17_out_7), .out_8(out_11),
    .read(decoder_2_out0));  // open: write, in_6
  new_memory_cell new_memory_cell_18 (
    .in_2(in_3), .in_3(WD_2), .clock(in_10), .out_7(new_memory_cell_18_out_7), .out_8(out_12),
    .read(decoder_2_out1), .write(decoder_3_out1), .in_6(_1));
  new_memory_cell new_memory_cell_19 (
    .in_2(in_3), .in_3(WD_2), .clock(in_10), .out_7(new_memory_cell_19_out_7), .out_8(out_13),
    .read(decoder_2_out2), .write(decoder_3_out2), .in_6(_2));
  new_memory_cell new_memory_cell_20 (
    .in_2(in_3), .in_3(WD_2), .clock(in_10), .out_7(new_memory_cell_20_out_7), .out_8(out_14),
    .read(decoder_2_out3), .write(decoder_3_out3), .in_6(_3));
  new_memory_cell new_memory_cell_21 (
    .in_2(in_3), .in_3(WD_2), .clock(in_10), .out_7(new_memory_cell_21_out_7), .out_8(out_15),
    .read(decoder_2_out4), .write(decoder_3_out4), .in_6(_4));
  new_memory_cell new_memory_cell_22 (
    .in_2(in_3), .in_3(WD_2), .clock(in_10), .out_7(new_memory_cell_22_out_7), .out_8(out_16),
    .read(decoder_2_out5), .write(decoder_3_out5), .in_6(_5));
  new_memory_cell new_memory_cell_23 (
    .in_2(in_3), .in_3(WD_2), .clock(in_10), .out_7(new_memory_cell_23_out_7), .out_8(out_17),
    .read(decoder_2_out6), .write(decoder_3_out6), .in_6(_6));
  new_memory_cell new_memory_cell_24 (
    .in_2(in_3), .in_3(WD_2), .clock(in_10), .out_7(new_memory_cell_24_out_7), .out_8(out_18),
    .read(decoder_2_out7), .write(decoder_3_out7), .in_6(_7));
  new_memory_cell new_memory_cell_25 (
    .in_2(in_3), .in_3(WD_2), .clock(in_10), .out_7(new_memory_cell_25_out_7), .out_8(out_19),
    .read(decoder_2_out8), .write(decoder_3_out8), .in_6(_8));
  new_memory_cell new_memory_cell_26 (
    .in_2(in_3), .in_3(WD_2), .clock(in_10), .out_7(new_memory_cell_26_out_7), .out_8(out_20),
    .read(decoder_2_out9), .write(decoder_3_out9), .in_6(_9));
  new_memory_cell new_memory_cell_27 (
    .in_2(in_3), .in_3(WD_2), .clock(in_10), .out_7(new_memory_cell_27_out_7), .out_8(out_21),
    .read(decoder_2_out10), .write(decoder_3_out10), .in_6(_10));
  new_memory_cell new_memory_cell_28 (
    .in_2(in_3), .in_3(WD_2), .clock(in_10), .out_7(new_memory_cell_28_out_7), .out_8(out_22),
    .read(decoder_2_out11), .write(decoder_3_out11), .in_6(_11));
  new_memory_cell new_memory_cell_29 (
    .in_2(in_3), .in_3(WD_2), .clock(in_10), .out_7(new_memory_cell_29_out_7), .out_8(out_23),
    .read(decoder_2_out12), .write(decoder_3_out12), .in_6(_12));
  new_memory_cell new_memory_cell_30 (
    .in_2(in_3), .in_3(WD_2), .clock(in_10), .out_7(new_memory_cell_30_out_7), .out_8(out_24),
    .read(decoder_2_out13), .write(decoder_3_out13), .in_6(_13));
  new_memory_cell new_memory_cell_31 (
    .in_2(in_3), .in_3(in_2), .clock(in_10), .out_7(new_memory_cell_31_out_7), .out_8(out_25),
    .read(decoder_2_out14), .write(decoder_3_out14), .in_6(write));
  new_memory_cell new_memory_cell_32 (
    .in_2(in_3), .in_3(WD_2), .clock(in_10), .out_7(new_memory_cell_32_out_7), .out_8(out_26),
    .read(decoder_2_out15), .write(decoder_3_out15), .in_6(_15));
  assign out_28 = new_memory_cell_18_out_7 | new_memory_cell_19_out_7 | new_memory_cell_20_out_7 | new_memory_cell_21_out_7 | new_memory_cell_22_out_7 | new_memory_cell_23_out_7 | new_memory_cell_24_out_7 | new_memory_cell_25_out_7 | new_memory_cell_26_out_7 | new_memory_cell_27_out_7 | new_memory_cell_28_out_7 | new_memory_cell_29_out_7 | new_memory_cell_30_out_7 | new_memory_cell_31_out_7 | new_memory_cell_32_out_7 | new_memory_cell_17_out_7;  // OR_Gate or_2, 16 bits wide

  // Other names for the same wires on the sheet: _14 = write; c = in_10; WD[15:0] = in_3; WD2[15:0] = WD_2;
  //   WD_FP[15:0] = in_2

  // Notes on the sheet:
  //   Is it call or return? Do we write R14?
  //   FP
  //   RD 1
  //   FP
  //   WD
  //   RD 2
  //   WD for FP(R 14)
endmodule

module Memory_Cell (
  input  read,
  input  [15:0] \input ,
  input  clock,
  input  write,
  output [15:0] out_5,
  output [15:0] out_6
);

  wire [15:0] multiplexer_1_out;

  Multiplexer #(.width(16)) multiplexer_1 (.in1(\input ), .out(multiplexer_1_out), .sel(write));  // open: in0, en
  Register #(.width(16)) register_1 (.D(multiplexer_1_out), .Q(out_6), .clk(clock));  // open: en, clr
  Multiplexer #(.width(16)) multiplexer_2 (.in0({16{1'b0}}), .in1(out_6), .out(out_5), .sel(read));  // open: en

  // Notes on the sheet:
  //   output
endmodule

module ASL (
  input  [15:0] in_1,
  output out_2,
  output [15:0] out_3
);


  assign out_2 = in_1[15];
  assign out_3 = {in_1[14:0], 1'b0};
endmodule

module Branching_Control (
  input  [15:0] in_1,
  input  [15:0] in_2,
  input  [7:0] o,
  input  [3:0] b_8_11,
  input  b_12,
  input  [4:0] cb,
  output [15:0] out_7,
  output branch
);

  wire _0010, _0011, _0100, _0101, _0110, _0111, _1001, _1011, _1101, _1111, not_1_out, not_2_out, not_4_out,
       not_6_out, not_7_out, not_8_out, not_10_out, not_12_out, not_14_out, not_16_out, not_18_out, or_2_out,
       or_3_out, or_4_out, or_6_out, or_7_out, or_8_out, xor_2_out, xor_3_out, xor_4_out, xor_5_out,
       xor_6_out, xor_7_out, xor_8_out;
  wire [7:0] negator_1_out;
  wire [15:0] add, b_0100, b_0101, b_0110, b_0111, b_1000, b_1001, b_1010, b_1011, b_1100, b_1101, b_1110,
       b_1111, minus, multiplexer_2_out, multiplexer_3_out, multiplexer_4_out, multiplexer_5_out,
       multiplexer_18_out, multiplexer_19_out, o_0100, o_0101, o_0110, o_0111, o_1000, o_1001, o_1010,
       o_1011, o_1100, o_1101, o_1110, o_1111, pc_o;

  Negator negator_1 (.in(o), .out(negator_1_out));
  Multiplexer #(.width(16)) multiplexer_1 (.in0(add), .in1(minus), .out(pc_o), .sel(o[7]));  // open: en
  Adder #(.width(16)) adder_1 (.a({{8{1'b0}}, o}), .b(in_1), .out(add));  // open: cin, cout
  Subtractor #(.width(16)) subtractor_1 (.a(in_1), .b({{8{1'b0}}, negator_1_out}), .out(minus));  // open: bin, bout
  not not_1 (not_1_out, cb[1]);
  not not_2 (not_2_out, cb[1]);
  Multiplexer #(.width(16)) multiplexer_2 (.in0(in_1), .in1(pc_o), .out(multiplexer_2_out), .sel(_0010));  // open: en
  xor xor_1 (_0010, cb[4], cb[2]);
  Multiplexer #(.width(16)) multiplexer_3 (.in0(in_1), .in1(pc_o), .out(multiplexer_3_out), .sel(_0011));  // open: en
  xor xor_2 (xor_2_out, cb[4], cb[2]);
  not not_3 (_0011, xor_2_out);
  Multiplexer #(.width(16)) multiplexer_4 (
    .in0(in_1), .in1(in_2), .out(multiplexer_4_out), .sel(xor_3_out));  // open: en
  xor xor_3 (xor_3_out, cb[4], cb[2]);
  Multiplexer #(.width(16)) multiplexer_5 (
    .in0(in_1), .in1(in_2), .out(multiplexer_5_out), .sel(not_4_out));  // open: en
  not not_4 (not_4_out, xor_4_out);
  xor xor_4 (xor_4_out, cb[4], cb[2]);
  Multiplexer #(.width(16)) multiplexer_6 (.in0(in_1), .in1(pc_o), .out(o_0100), .sel(_0100));  // open: en
  xor xor_5 (xor_5_out, cb[4], cb[2]);
  or or_1 (_0100, xor_5_out, cb[3]);
  Multiplexer #(.width(16)) multiplexer_7 (.in0(in_1), .in1(in_2), .out(b_0100), .sel(or_2_out));  // open: en
  xor xor_6 (xor_6_out, cb[4], cb[2]);
  or or_2 (or_2_out, xor_6_out, cb[3]);
  xor xor_7 (xor_7_out, cb[4], cb[2]);
  not not_5 (_0101, or_3_out);
  or or_3 (or_3_out, xor_7_out, cb[3]);
  xor xor_8 (xor_8_out, cb[4], cb[2]);
  or or_4 (or_4_out, xor_8_out, cb[3]);
  not not_6 (not_6_out, or_4_out);
  not not_7 (not_7_out, cb[1]);
  or or_5 (_0110, not_7_out, cb[3]);
  not not_8 (not_8_out, cb[1]);
  or or_6 (or_6_out, not_8_out, cb[3]);
  not not_9 (_0111, or_7_out);
  or or_7 (or_7_out, not_1_out, cb[3]);
  not not_10 (not_10_out, or_8_out);
  or or_8 (or_8_out, not_2_out, cb[3]);
  Multiplexer #(.width(16)) multiplexer_8 (.in0(in_1), .in1(pc_o), .out(o_1100), .sel(cb[4]));  // open: en
  Multiplexer #(.width(16)) multiplexer_9 (.in0(in_1), .in1(in_2), .out(b_1100), .sel(cb[4]));  // open: en
  Multiplexer #(.width(16)) multiplexer_10 (.in0(in_1), .in1(pc_o), .out(o_1110), .sel(cb[2]));  // open: en
  Multiplexer #(.width(16)) multiplexer_11 (.in0(in_1), .in1(in_2), .out(b_1110), .sel(cb[2]));  // open: en
  Multiplexer #(.width(16)) multiplexer_12 (.in0(in_1), .in1(pc_o), .out(o_0101), .sel(_0101));  // open: en
  Multiplexer #(.width(16)) multiplexer_13 (.in0(in_1), .in1(in_2), .out(b_0101), .sel(not_6_out));  // open: en
  Multiplexer #(.width(16)) multiplexer_14 (.in0(in_1), .in1(pc_o), .out(o_0110), .sel(_0110));  // open: en
  Multiplexer #(.width(16)) multiplexer_15 (.in0(in_1), .in1(in_2), .out(b_0110), .sel(or_6_out));  // open: en
  Multiplexer #(.width(16)) multiplexer_16 (.in0(in_1), .in1(pc_o), .out(o_0111), .sel(_0111));  // open: en
  Multiplexer #(.width(16)) multiplexer_17 (.in0(in_1), .in1(in_2), .out(b_0111), .sel(not_10_out));  // open: en
  Multiplexer #(.select(4), .width(16)) multiplexer_18 (
    .in0(pc_o), .in2(multiplexer_2_out), .in3(multiplexer_3_out), .in4(o_0100), .in5(o_0101), .in6(o_0110),
    .in7(o_0111), .in8(o_1000), .in9(o_1001), .in10(o_1010), .in11(o_1011), .in12(o_1100), .in13(o_1101),
    .in14(o_1110), .in15(o_1111), .out(multiplexer_18_out), .sel(b_8_11));  // open: in1, en
  Multiplexer #(.select(4), .width(16)) multiplexer_19 (
    .in0(in_2), .in2(multiplexer_4_out), .in3(multiplexer_5_out), .in4(b_0100), .in5(b_0101), .in6(b_0110),
    .in7(b_0111), .in8(b_1000), .in9(b_1001), .in10(b_1010), .in11(b_1011), .in12(b_1100), .in13(b_1101),
    .in14(b_1110), .in15(b_1111), .out(multiplexer_19_out), .sel(b_8_11));  // open: in1, en
  Multiplexer #(.width(16)) multiplexer_20 (.in0(in_1), .in1(pc_o), .out(o_1000), .sel(cb[3]));  // open: en
  Multiplexer #(.width(16)) multiplexer_21 (.in0(in_1), .in1(in_2), .out(b_1000), .sel(cb[3]));  // open: en
  Multiplexer #(.width(16)) multiplexer_22 (.in0(in_1), .in1(pc_o), .out(o_1001), .sel(_1001));  // open: en
  not not_11 (_1001, cb[3]);
  Multiplexer #(.width(16)) multiplexer_23 (.in0(in_1), .in1(in_2), .out(b_1001), .sel(not_12_out));  // open: en
  not not_12 (not_12_out, cb[3]);
  Multiplexer #(.width(16)) multiplexer_24 (.in0(in_1), .in1(pc_o), .out(o_1010), .sel(cb[1]));  // open: en
  Multiplexer #(.width(16)) multiplexer_25 (.in0(in_1), .in1(in_2), .out(b_1010), .sel(cb[1]));  // open: en
  Multiplexer #(.width(16)) multiplexer_26 (.in0(in_1), .in1(pc_o), .out(o_1011), .sel(_1011));  // open: en
  not not_13 (_1011, cb[1]);
  Multiplexer #(.width(16)) multiplexer_27 (.in0(in_1), .in1(in_2), .out(b_1011), .sel(not_14_out));  // open: en
  not not_14 (not_14_out, cb[1]);
  Multiplexer #(.width(16)) multiplexer_28 (.in0(in_1), .in1(pc_o), .out(o_1101), .sel(_1101));  // open: en
  not not_15 (_1101, cb[4]);
  Multiplexer #(.width(16)) multiplexer_29 (.in0(in_1), .in1(in_2), .out(b_1101), .sel(not_16_out));  // open: en
  not not_16 (not_16_out, cb[4]);
  Multiplexer #(.width(16)) multiplexer_30 (.in0(in_1), .in1(pc_o), .out(o_1111), .sel(_1111));  // open: en
  not not_17 (_1111, cb[2]);
  Multiplexer #(.width(16)) multiplexer_31 (.in0(in_1), .in1(in_2), .out(b_1111), .sel(not_18_out));  // open: en
  not not_18 (not_18_out, cb[2]);
  Multiplexer #(.width(16)) multiplexer_32 (
    .in0(multiplexer_18_out), .in1(multiplexer_19_out), .out(out_7), .sel(b_12));  // open: en
  Multiplexer #(.select(4)) multiplexer_33 (
    .in0(1'b1), .in1(1'b0), .in2(_0010), .in3(_0011), .in4(_0100), .in5(_0101), .in6(_0110), .in7(_0111),
    .in8(cb[3]), .in9(_1001), .in10(cb[1]), .in11(_1011), .in12(cb[4]), .in13(_1101), .in14(cb[2]),
    .in15(_1111), .out(branch), .sel(b_8_11));  // open: en

  // Other names for the same wires on the sheet: _8_11[3:0] = b_8_11; b[15:0] = in_2; _1010 = cb[1]; c = cb[1];
  //   _1110 = cb[2]; v = cb[2]; _1000 = cb[3]; z = cb[3]; _1100 = cb[4]; s = cb[4]; current_PC[15:0] = in_1

  // Notes on the sheet:
  //   R b
  //   current flags
  //   c
  //   v
  //   z
  //   s
  //   0100
  //   0101
  //   0110
  //   0111
  //   1100
  //   1110
  //   current PC
  //   1000
  //   1001
  //   1010
  //   1011
  //   1101
  //   1111
  //   O
  //   b
endmodule

module flags_manipulation (
  input  [3:0] d_8_11,
  input  [7:0] op_code_2_0_7,
  input  [4:0] current_flags,
  output [4:0] out_4
);

  wire [4:0] and_1_out, not_1_out, or_1_out;

  assign not_1_out = ~{op_code_2_0_7[0], op_code_2_0_7[1], op_code_2_0_7[2], op_code_2_0_7[3], d_8_11[0]};  // NOT_Gate not_1, 5 bits wide
  assign or_1_out = {op_code_2_0_7[0], op_code_2_0_7[1], op_code_2_0_7[2], op_code_2_0_7[3], d_8_11[0]} | current_flags;  // OR_Gate or_1, 5 bits wide
  assign and_1_out = not_1_out & current_flags;  // AND_Gate and_1, 5 bits wide
  Multiplexer #(.select(3), .width(5)) multiplexer_1 (
    .in0(or_1_out),
    .in2({op_code_2_0_7[0], op_code_2_0_7[1], op_code_2_0_7[2], op_code_2_0_7[3], d_8_11[0]}),
    .in4(and_1_out),
    .in6({op_code_2_0_7[0], op_code_2_0_7[1], op_code_2_0_7[2], op_code_2_0_7[3], current_flags[0]}),
    .out(out_4), .sel(d_8_11[3:1]));  // open: in1, in3, in5, in7, en

  // Notes on the sheet:
  //   flag op
  //   v4
  //   v(0-3)
  //   F
  //   v
endmodule

module HERA_Memory (
  input  [15:0] in_1,
  input  [15:0] store,
  input  clock,
  input  in_4,
  output [15:0] out_5
);

  RAM #(.addrWidth(16), .dataWidth(16), .bus("separate")) ram_1 (
    .addr(in_1), .din(store), .data(out_5), .str(in_4), .clk(clock));  // open: sel, ld, clr

  // Notes on the sheet:
  //   16 x 2^16 bit
  //   read without clock
  //   enable write with clock
  //   load
endmodule

module new_memory_cell (
  input  read,
  input  [15:0] in_2,
  input  [15:0] in_3,
  input  clock,
  input  write,
  input  in_6,
  output [15:0] out_7,
  output [15:0] out_8
);

  wire [15:0] multiplexer_1_out;

  Multiplexer #(.select(2), .width(16)) multiplexer_1 (
    .in1(in_3), .in2(in_2), .out(multiplexer_1_out), .sel({write, in_6}));  // open: in0, in3, en
  Register #(.width(16)) register_1 (.D(multiplexer_1_out), .Q(out_8), .clk(clock));  // open: en, clr
  Multiplexer #(.width(16)) multiplexer_2 (.in0({16{1'b0}}), .in1(out_8), .out(out_7), .sel(read));  // open: en

  // Notes on the sheet:
  //   input
  //   output
endmodule
